# Fritzing sketch Electric circuit (saved by Fritzing 0.9.3b)
breadboards: 1

parts:
  Part1 = Arduino Uno (Rev3) - ICSP
  Part2 = FC-03 [chip_label=FC-03]
  Part3 = FC-03 [chip_label=FC-03]
  IC1 = Voltage Regulator [package=to-220-alt]
  Part4 = Bluetooth HC-05 Macho
  L298N1 = L298N DC motor driver
  LED2 = RGB LED - (4 legs) [package="5 mm [THT]"]
  LED3 = LED - 3mm [color="Red (633nm)" package="3 mm [THT]"]
  VCC1 = Battery block 9V
  R1 = Resistor [tolerance=±5% resistance=330 package=THT]
  R2 = Resistor [tolerance=±5% resistance=330 package=THT]
  R3 = Resistor [tolerance=±5% resistance=330 package=THT]
  R4 = Resistor [tolerance=±5% resistance=330 package=THT]
  J1 = Basic Servo
  J2 = Basic Servo
  R6 = Resistor [tolerance=±5% resistance=330 package=THT]
  R5 = Resistor [tolerance=±5% resistance=330 package=THT]
  U1 = Header 6 [package=1x06_smd_straight_alt]
  U2 = Header 6 [package=1x06_smd_straight_alt]
  M3 = Getriebemotor
  M4 = Getriebemotor

nets:
  N1: Part1.A4/SDA, Part2.D0
  N2: Part1.A5/SCL, Part3.D0
  N3: Part1.D8, U2.2
  N4: Part1.D9_PWM, U2.3
  N5: Part1.D10_PWM/SS, U2.4
  N6: Part1.D11_PWM/MOSI, U2.5
  N7: Part1.D12/MISO, J1.pulse
  N8: Part1.D13/SCK, J2.pulse
  N9: Part1.D0/RX, Part4.TXD
  N10: Part1.D1/TX, R6.Pin_0
  N11: Part1.D2, Part4.State
  N12: Part1.D3_PWM, U2.1
  N13: Part1.D5_PWM, U2.6
  N14: Part1.D6_PWM, R1.Pin_0
  N15: Part1.D7, R2.Pin_0
  GND: Part1.GND, Part2.GND, Part3.GND, IC1.IN, Part4.GND, L298N1.GND, LED3.cathode, VCC1.-, J1.gnd, J2.gnd, R5.Pin_0
  VCC: Part1.VIN, Part2.VCC, Part3.VCC, IC1.OUT, Part4.VCC, L298N1.5V, LED2.common_anode, R3.Pin_0, R4.Pin_1, J1.vcc, J2.vcc
  GND_2: IC1.GND, L298N1.12V, VCC1.+
  N16: L298N1.OUT1, M4.pin_2
  N17: L298N1.OUT2, M4.pin_1
  N18: L298N1.OUT3, M3.pin_1
  N19: L298N1.OUT4, M3.pin_2
  N20: L298N1.ENA, U1.6
  N21: L298N1.ENB, U1.1
  N22: L298N1.IN1, U1.5
  N23: L298N1.IN2, U1.4
  N24: L298N1.IN3, U1.3
  N25: L298N1.IN4, U1.2
  N26: LED2.red_cathode, R3.Pin_1
  N27: LED2.green_cathode, R1.Pin_1
  N28: LED2.blue_cathode, R2.Pin_1
  N29: LED3.anode, R4.Pin_0
  N30: R6.Pin_1, R5.Pin_1

notes:
  12V

custom parts:
  FC-03: FC-03, LM393 IR Speed Sensor Encoder
  L298N DC motor driver: 2x DC motor driver with 78M05 positive voltage regulator (7..35 V) L298N: max 46 V, 2 A Set 5 V Enable jumper to enable 5 V regultor (needed for the L298N) and +5 V output at screw terminal or supply external +5 V at screw terminal Set ENA and/or ENB to +5 V to enable motor permanently or supply ENA and/or ENB with PWM signal IN1 and IN2 set rotation directory for motor A (OUT1/OUT2) IN2 and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
